// Logisim project 6.circ as structural Verilog: 1 circuit, main circuit main
module main (
  input  A0,
  input  A1,
  input  A2,
  input  A3,
  output C0,
  output C1,
  output C2,
  output C3
);

  not not_1 (C0, A0);
  not not_2 (C1, A1);
  not not_3 (C2, A2);
  not not_4 (C3, A3);
endmodule
