// Logisim project circ.circ as structural Verilog: 1 circuit, main circuit main
module main (
  input  A0,
  input  B0,
  input  B1,
  input  B2,
  input  A1,
  input  A2,
  output S0,
  output S1,
  output S2,
  output C2
);

  wire and_1_out, and_3_out, and_4_out, and_6_out, or_1_out, or_2_out, or_3_out;

  and and_1 (and_1_out, A0, B0);
  or or_1 (or_1_out, A0, B0);
  and and_2 (S0, or_1_out, and_1_out);
  or or_2 (or_2_out, and_1_out, A1);
  and and_3 (and_3_out, and_1_out, A1);
  and and_4 (and_4_out, or_2_out, and_3_out);
  or or_3 (or_3_out, and_3_out, A2);
  and and_5 (C2, and_3_out, A2);
  or or_4 (S1, B1, and_4_out);
  and and_6 (and_6_out, or_3_out, C2);
  or or_5 (S2, B2, and_6_out);
endmodule
