// Logisim project circuitos cuestionario.circ as structural Verilog: 1 circuit, main circuit main
module main (
  input  A0,
  input  A1,
  input  A2,
  input  A3,
  input  B0,
  input  B1,
  input  B2,
  input  B3,
  output C0,
  output C1,
  output C2,
  output C3
);

  or or_1 (C0, A0, B0);
  or or_2 (C1, A1, B1);
  or or_3 (C2, A2, B2);
  or or_4 (C3, A3, B3);
endmodule
